// Logisim project adder.circ as structural Verilog
module adder (
  input  Cin,
  input  a,
  input  b,
  output Sum,
  output Cout
);

  wire and_1_out, and_2_out, xor_1_out;

  and and_1 (and_1_out, b, a);
  or or_1 (Cout, and_1_out, and_2_out);
  xor xor_1 (xor_1_out, a, b);
  and and_2 (and_2_out, xor_1_out, Cin);
  xor xor_2 (Sum, Cin, xor_1_out);
endmodule

module _1_Bit_ALU (
  input  Binvert,
  input  CarryIn,
  input  a,
  input  b,
  output Result,
  output CarryOut
);

  wire xor_1_out;

  xor xor_1 (xor_1_out, Binvert, b);
  adder adder_1 (.Cin(CarryIn), .a(a), .b(xor_1_out), .Sum(Result), .Cout(CarryOut));
endmodule

module _16_Bit_ALU (
  input  sub,
  input  [15:0] A,
  input  [15:0] B,
  output [15:0] result,
  output ovf
);

  wire n1_bit_alu_1_carryout, n1_bit_alu_2_carryout, n1_bit_alu_3_carryout, n1_bit_alu_4_carryout,
       n1_bit_alu_5_carryout, n1_bit_alu_6_carryout, n1_bit_alu_7_carryout, n1_bit_alu_8_carryout,
       n1_bit_alu_9_carryout, n1_bit_alu_10_carryout, n1_bit_alu_11_carryout, n1_bit_alu_12_carryout,
       n1_bit_alu_13_carryout, n1_bit_alu_14_carryout, n1_bit_alu_15_carryout, n1_bit_alu_16_carryout;

  _1_Bit_ALU u_1_bit_alu_1 (
    .a(A[0]), .b(B[0]), .Result(result[0]), .Binvert(sub), .CarryIn(sub), .CarryOut(n1_bit_alu_1_carryout));
  _1_Bit_ALU u_1_bit_alu_2 (
    .a(A[1]), .b(B[1]), .Result(result[1]), .Binvert(sub), .CarryIn(n1_bit_alu_1_carryout),
    .CarryOut(n1_bit_alu_2_carryout));
  _1_Bit_ALU u_1_bit_alu_3 (
    .a(A[2]), .b(B[2]), .Result(result[2]), .Binvert(sub), .CarryIn(n1_bit_alu_2_carryout),
    .CarryOut(n1_bit_alu_3_carryout));
  _1_Bit_ALU u_1_bit_alu_4 (
    .a(A[3]), .b(B[3]), .Result(result[3]), .Binvert(sub), .CarryIn(n1_bit_alu_3_carryout),
    .CarryOut(n1_bit_alu_4_carryout));
  _1_Bit_ALU u_1_bit_alu_5 (
    .a(A[4]), .b(B[4]), .Result(result[4]), .Binvert(sub), .CarryIn(n1_bit_alu_4_carryout),
    .CarryOut(n1_bit_alu_5_carryout));
  _1_Bit_ALU u_1_bit_alu_6 (
    .a(A[5]), .b(B[5]), .Result(result[5]), .Binvert(sub), .CarryIn(n1_bit_alu_5_carryout),
    .CarryOut(n1_bit_alu_6_carryout));
  _1_Bit_ALU u_1_bit_alu_7 (
    .a(A[6]), .b(B[6]), .Result(result[6]), .Binvert(sub), .CarryIn(n1_bit_alu_6_carryout),
    .CarryOut(n1_bit_alu_7_carryout));
  _1_Bit_ALU u_1_bit_alu_8 (
    .a(A[7]), .b(B[7]), .Result(result[7]), .Binvert(sub), .CarryIn(n1_bit_alu_7_carryout),
    .CarryOut(n1_bit_alu_8_carryout));
  _1_Bit_ALU u_1_bit_alu_9 (
    .a(A[8]), .b(B[8]), .Result(result[8]), .Binvert(sub), .CarryIn(n1_bit_alu_8_carryout),
    .CarryOut(n1_bit_alu_9_carryout));
  _1_Bit_ALU u_1_bit_alu_10 (
    .a(A[9]), .b(B[9]), .Result(result[9]), .Binvert(sub), .CarryIn(n1_bit_alu_9_carryout),
    .CarryOut(n1_bit_alu_10_carryout));
  _1_Bit_ALU u_1_bit_alu_11 (
    .a(A[10]), .b(B[10]), .Result(result[10]), .Binvert(sub), .CarryIn(n1_bit_alu_10_carryout),
    .CarryOut(n1_bit_alu_11_carryout));
  _1_Bit_ALU u_1_bit_alu_12 (
    .a(A[11]), .b(B[11]), .Result(result[11]), .Binvert(sub), .CarryIn(n1_bit_alu_11_carryout),
    .CarryOut(n1_bit_alu_12_carryout));
  _1_Bit_ALU u_1_bit_alu_13 (
    .a(A[12]), .b(B[12]), .Result(result[12]), .Binvert(sub), .CarryIn(n1_bit_alu_12_carryout),
    .CarryOut(n1_bit_alu_13_carryout));
  _1_Bit_ALU u_1_bit_alu_14 (
    .a(A[13]), .b(B[13]), .Result(result[13]), .Binvert(sub), .CarryIn(n1_bit_alu_13_carryout),
    .CarryOut(n1_bit_alu_14_carryout));
  _1_Bit_ALU u_1_bit_alu_15 (
    .a(A[14]), .b(B[14]), .Result(result[14]), .Binvert(sub), .CarryIn(n1_bit_alu_14_carryout),
    .CarryOut(n1_bit_alu_15_carryout));
  _1_Bit_ALU u_1_bit_alu_16 (
    .a(A[15]), .b(B[15]), .Result(result[15]), .Binvert(sub), .CarryIn(n1_bit_alu_15_carryout),
    .CarryOut(n1_bit_alu_16_carryout));
  xor xor_1 (ovf, n1_bit_alu_15_carryout, n1_bit_alu_16_carryout);
endmodule
