// Logisim project circuit1a.circ as structural Verilog: 2 circuits, main circuit circuit1a
module main (
);

  wire and_1_out, undriven, undriven_2, undriven_3;

  and and_1 (and_1_out, undriven_2, undriven_3);
  // OR_Gate or_1 has open pins: in0=undriven, in1=and_1_out, out=open

  // Notes on the sheet:
  //   A
  //   B
  //   C
endmodule

module circuit1a (
  input  A,
  input  B,
  input  C,
  output out
);

  wire and_1_out;

  and and_1 (and_1_out, B, C);
  or or_1 (out, A, and_1_out);
endmodule
