// Logisim project fsm.circ as structural Verilog: 1 circuit, main circuit fsm
module fsm (
  input  in2,
  input  in1,
  output out1,
  output out2
);

  wire _00_diff_out, _00_eq_out, _01_diff_out, _01_eq_out, _10_diff_out, _10_eq_out, _11_diff_out,
       _11_eq_out, clock_1_out, not_1_out, not_2_out, not_3_out, not_4_out, not_5_out, not_6_out, or_1_out,
       or_2_out, s0_q, s1_q, xor_1_out;

  xor xor_1 (xor_1_out, in2, in1);
  not not_1 (not_1_out, s1_q);
  not not_2 (not_2_out, xor_1_out);
  not not_3 (not_3_out, xor_1_out);
  not not_4 (not_4_out, xor_1_out);
  not not_5 (not_5_out, xor_1_out);
  not not_6 (not_6_out, s0_q);
  and _00_eq (_00_eq_out, not_1_out, not_6_out, not_2_out);
  and _00_diff (_00_diff_out, not_1_out, not_6_out, xor_1_out);
  and _01_eq (_01_eq_out, not_1_out, s0_q, not_3_out);
  and _01_diff (_01_diff_out, not_1_out, s0_q, xor_1_out);
  and _10_eq (_10_eq_out, s1_q, not_6_out, not_4_out);
  and _10_diff (_10_diff_out, s1_q, not_6_out, xor_1_out);
  and _11_eq (_11_eq_out, s1_q, s0_q, not_5_out);
  and _11_diff (_11_diff_out, s1_q, s0_q, xor_1_out);
  Clock clock_1 (.out(clock_1_out));
  or or_1 (or_1_out, _00_eq_out, _01_eq_out, _01_diff_out, _10_diff_out, _11_eq_out, _11_diff_out);
  or or_2 (or_2_out, _00_diff_out, _01_eq_out, _10_eq_out, _11_eq_out);
  D_Flip_Flop s1 (.clk(clock_1_out), .D(or_1_out), .Q(s1_q));  // open: Qn, preset, en, reset
  D_Flip_Flop s0 (.clk(clock_1_out), .D(or_2_out), .Q(s0_q));  // open: Qn, preset, en, reset
  and and_1 (out1, s1_q, s0_q);
  // AND_Gate and_2 has open pins: in0=s1_q, in1=s0_q, out=open
endmodule
