// Logisim project hw4.circ as structural Verilog: 4 circuits, main circuit Processor
module Processor (
  input  reset
);

  wire alu_1_zero, and_1_out, and_2_out, clock_1_out, control_1_aluin, control_1_branch, control_1_input,
       control_1_jal, control_1_jump, control_1_memtoreg, control_1_memwrite, control_1_output,
       control_1_regdst, control_1_regwrite, keyboard_1_avail, not_1_out, not_2_out;
  wire [2:0] multiplexer_1_out, multiplexer_3_out;
  wire [6:0] bit_extender_5_out, keyboard_1_data;
  wire [7:0] bit_extender_2_out, multiplexer_2_out;
  wire [11:0] rom_1_data;
  wire [15:0] adder_1_out, adder_2_out, alu_1_dataout, bit_extender_1_out, bit_extender_3_out,
       bit_extender_4_out, multiplexer_4_out, multiplexer_5_out, multiplexer_6_out, multiplexer_7_out,
       multiplexer_8_out, multiplexer_9_out, multiplexer_10_out, PC_q, ram_1_data, RegisterFile_out1,
       RegisterFile_out2;
  wire [15:12] rom_1_data_2;

  Clock clock_1 (.out(clock_1_out));
  Register #(.width(16)) PC (.D(multiplexer_10_out), .Q(PC_q), .clk(clock_1_out), .clr(reset));  // open: en
  Keyboard keyboard_1 (.re(clock_1_out), .clr(reset), .avail(keyboard_1_avail), .data(keyboard_1_data));  // open: clk
  assign bit_extender_1_out = {{4{1'b0}}, rom_1_data};  // Bit_Extender bit_extender_1
  Adder #(.width(16)) adder_1 (.a(PC_q), .b(16'h1), .out(adder_1_out));  // open: cin, cout
  ROM #(.addrWidth(16), .dataWidth(16)) rom_1 (.addr(PC_q), .data({rom_1_data_2, rom_1_data}));  // open: sel
  Multiplexer #(.width(3), .enable("false")) multiplexer_1 (
    .in0(rom_1_data[8:6]), .in1(rom_1_data[5:3]), .out(multiplexer_1_out), .sel(control_1_regdst));
  assign bit_extender_2_out = {{1{1'b0}}, keyboard_1_data};  // Bit_Extender bit_extender_2
  Control control_1 (
    .Op(rom_1_data_2), .RegDst(control_1_regdst), .Branch(control_1_branch), .MemWrite(control_1_memwrite),
    .Jump(control_1_jump), .ALUin(control_1_aluin), .RegWrite(control_1_regwrite),
    .MemToReg(control_1_memtoreg), .jal(control_1_jal), .\input (control_1_input), .\output (control_1_output));
  assign bit_extender_3_out = {{10{rom_1_data[5]}}, rom_1_data[5:0]};  // Bit_Extender bit_extender_3
  not not_1 (not_1_out, clock_1_out);
  Multiplexer #(.width(8), .enable("false")) multiplexer_2 (
    .in0(8'h80), .in1(bit_extender_2_out), .out(multiplexer_2_out), .sel(keyboard_1_avail));
  Multiplexer #(.width(3), .enable("false")) multiplexer_3 (
    .in0(multiplexer_1_out), .in1(3'b111), .out(multiplexer_3_out), .sel(control_1_jal));
  Multiplexer #(.width(16), .enable("false")) multiplexer_4 (
    .in0(multiplexer_7_out), .in1(bit_extender_4_out), .out(multiplexer_4_out), .sel(control_1_input));
  assign bit_extender_4_out = {{8{1'b0}}, multiplexer_2_out};  // Bit_Extender bit_extender_4
  and and_1 (and_1_out, control_1_regwrite, not_1_out);
  RegisterFile RegisterFile (
    .RegWrite(and_1_out), .Write_Data(multiplexer_4_out), .Read_Reg_1(rom_1_data[11:9]),
    .Read_Reg_2(rom_1_data[8:6]), .reset(reset), .out1(RegisterFile_out1), .out2(RegisterFile_out2),
    .Write_Reg(multiplexer_3_out), .clock(clock_1_out));
  Multiplexer #(.width(16), .enable("false")) multiplexer_5 (
    .in0(RegisterFile_out2), .in1(bit_extender_3_out), .out(multiplexer_5_out), .sel(control_1_aluin));
  Multiplexer #(.width(16), .enable("false")) multiplexer_6 (
    .in0(bit_extender_1_out), .in1(RegisterFile_out1), .out(multiplexer_6_out), .sel(control_1_regdst));
  Adder #(.width(16)) adder_2 (.a(adder_1_out), .b(bit_extender_3_out), .out(adder_2_out));  // open: cin, cout
  ALU alu_1 (
    .in1___rs(RegisterFile_out1), .dataOut(alu_1_dataout), .in2___rt_imm(multiplexer_5_out),
    .Opcode(rom_1_data_2), .Zero(alu_1_zero));
  Multiplexer #(.width(16), .enable("false")) multiplexer_7 (
    .in0(multiplexer_9_out), .in1(adder_1_out), .out(multiplexer_7_out), .sel(control_1_jal));
  Bit_Extender #(.in_width(16), .out_width(7)) bit_extender_5 (.in(RegisterFile_out1), .out(bit_extender_5_out));
  TTY #(.rows(13), .cols(80), .trigger("falling")) tty_1 (
    .data(bit_extender_5_out), .clk(clock_1_out), .we(control_1_output), .clr(reset));
  and and_2 (and_2_out, control_1_branch, alu_1_zero);
  not not_2 (not_2_out, clock_1_out);
  Multiplexer #(.width(16), .enable("false")) multiplexer_8 (
    .in0(adder_1_out), .in1(adder_2_out), .out(multiplexer_8_out), .sel(and_2_out));
  Multiplexer #(.width(16), .enable("false")) multiplexer_9 (
    .in0(alu_1_dataout), .in1(ram_1_data), .out(multiplexer_9_out), .sel(control_1_memtoreg));
  RAM #(.addrWidth(16), .dataWidth(16), .bus("separate")) ram_1 (
    .addr(alu_1_dataout), .din(RegisterFile_out2), .data(ram_1_data), .str(control_1_memwrite),
    .clk(not_2_out));  // open: sel, ld, clr
  Multiplexer #(.width(16), .enable("false")) multiplexer_10 (
    .in0(multiplexer_8_out), .in1(multiplexer_6_out), .out(multiplexer_10_out), .sel(control_1_jump));

  // Notes on the sheet:
  //   contents of rom_1 (hex, n*v repeats v):
  //   4*0 2104
endmodule

module RegisterFile (
  input  RegWrite,
  input  [15:0] Write_Data,
  input  [2:0] Read_Reg_1,
  input  [2:0] Read_Reg_2,
  input  [2:0] Write_Reg,
  input  clock,
  input  reset,
  output [15:0] out1,
  output [15:0] out2
);

  wire demultiplexer_1_out0, demultiplexer_1_out1, demultiplexer_1_out2, demultiplexer_1_out3,
       demultiplexer_1_out4, demultiplexer_1_out5, demultiplexer_1_out6, demultiplexer_1_out7;
  wire [15:0] Clock_Trigger_q, r0_2_q, r1_2_q, r2_2_q, r3_q, r4_2_q, r5_q, r6_q, r7_q;

  // Probe on r0_2_q
  Register #(.width(16), .trigger("falling")) Clock_Trigger (
    .D(Write_Data), .Q(Clock_Trigger_q), .clk(clock), .clr(reset));  // open: en
  Demultiplexer #(.select(3)) demultiplexer_1 (
    .out0(demultiplexer_1_out0), .out1(demultiplexer_1_out1), .out2(demultiplexer_1_out2),
    .out3(demultiplexer_1_out3), .out4(demultiplexer_1_out4), .out5(demultiplexer_1_out5),
    .out6(demultiplexer_1_out6), .out7(demultiplexer_1_out7), .in(RegWrite), .sel(Write_Reg));  // open: en
  // Probe on r1_2_q
  // Probe on r2_2_q
  Register #(.width(16), .trigger("high")) r0_2 (
    .D({16{1'b0}}), .Q(r0_2_q), .clk(demultiplexer_1_out0), .clr(reset));  // open: en
  Register #(.width(16), .trigger("high")) r1_2 (
    .D(Clock_Trigger_q), .Q(r1_2_q), .clk(demultiplexer_1_out1), .clr(reset));  // open: en
  Register #(.width(16), .trigger("high")) r2_2 (
    .D(Clock_Trigger_q), .Q(r2_2_q), .clk(demultiplexer_1_out2), .clr(reset));  // open: en
  Register #(.width(16), .trigger("high")) r3 (
    .D(Clock_Trigger_q), .Q(r3_q), .clk(demultiplexer_1_out3), .clr(reset));  // open: en
  // Probe on r3_q
  // Probe on r4_2_q
  Register #(.width(16), .trigger("high")) r4_2 (
    .D(Clock_Trigger_q), .Q(r4_2_q), .clk(demultiplexer_1_out4), .clr(reset));  // open: en
  Register #(.width(16), .trigger("high")) r5 (
    .D(Clock_Trigger_q), .Q(r5_q), .clk(demultiplexer_1_out5), .clr(reset));  // open: en
  Register #(.width(16), .trigger("high")) r6 (
    .D(Clock_Trigger_q), .Q(r6_q), .clk(demultiplexer_1_out6), .clr(reset));  // open: en
  Register #(.width(16), .trigger("high")) r7 (
    .D(Clock_Trigger_q), .Q(r7_q), .clk(demultiplexer_1_out7), .clr(reset));  // open: en
  // Probe on r5_q
  // Probe on r6_q
  Multiplexer #(.select(3), .width(16), .enable("false")) multiplexer_1 (
    .in0(r0_2_q), .in1(r1_2_q), .in2(r2_2_q), .in3(r3_q), .in4(r4_2_q), .in5(r5_q), .in6(r6_q), .in7(r7_q),
    .out(out1), .sel(Read_Reg_1));
  Multiplexer #(.select(3), .width(16), .enable("false")) multiplexer_2 (
    .in0(r0_2_q), .in1(r1_2_q), .in2(r2_2_q), .in3(r3_q), .in4(r4_2_q), .in5(r5_q), .in6(r6_q), .in7(r7_q),
    .out(out2), .sel(Read_Reg_2));
  // Probe on r7_q
endmodule

module ALU (
  input  [15:0] in1___rs,
  input  [15:0] in2___rt_imm,
  input  [3:0] Opcode,
  output Zero,
  output [15:0] dataOut
);

  wire comparator_1_eq, comparator_1_lt;
  wire [2:0] bit_extender_1_out;
  wire [3:0] bit_extender_2_out;
  wire [15:0] adder_1_out, bit_extender_3_out, bit_extender_4_out, not_1_out, shifter_1_out, shifter_2_out,
       subtractor_1_out, xor_1_out;

  assign xor_1_out = in1___rs ^ in2___rt_imm;  // XOR_Gate xor_1, 16 bits wide
  assign not_1_out = ~in1___rs;  // NOT_Gate not_1, 16 bits wide
  Adder #(.width(16)) adder_1 (.a(in1___rs), .b(in2___rt_imm), .out(adder_1_out));  // open: cin, cout
  Subtractor #(.width(16)) subtractor_1 (.a(in1___rs), .b(in2___rt_imm), .out(subtractor_1_out));  // open: bin, bout
  Bit_Extender #(.in_width(16), .out_width(3)) bit_extender_1 (.in(in2___rt_imm), .out(bit_extender_1_out));
  assign bit_extender_2_out = {{1{1'b0}}, bit_extender_1_out};  // Bit_Extender bit_extender_2
  Comparator #(.width(16)) comparator_1 (
    .a(in1___rs), .b(in2___rt_imm), .eq(comparator_1_eq), .lt(comparator_1_lt));  // open: gt
  Shifter #(.width(16), .shift("ar")) shifter_1 (.in(in1___rs), .\dist (bit_extender_2_out), .out(shifter_1_out));
  Shifter #(.width(16)) shifter_2 (.in(in1___rs), .\dist (bit_extender_2_out), .out(shifter_2_out));
  assign bit_extender_3_out = {{15{1'b0}}, comparator_1_eq};  // Bit_Extender bit_extender_3
  assign bit_extender_4_out = {{15{1'b0}}, comparator_1_lt};  // Bit_Extender bit_extender_4
  Multiplexer #(.select(4), .width(16)) multiplexer_1 (
    .in0(not_1_out), .in1(xor_1_out), .in2(adder_1_out), .in3(adder_1_out), .in4(subtractor_1_out),
    .in5(shifter_1_out), .in6(shifter_2_out), .in7(adder_1_out), .in8(adder_1_out), .in9({16{1'b0}}),
    .in10({16{1'b0}}), .in11({16{1'b0}}), .in12(bit_extender_3_out), .in13(bit_extender_4_out),
    .in14({16{1'b0}}), .in15(in1___rs), .out(dataOut), .sel(Opcode));  // open: en
  nor Z (Zero, dataOut[0], dataOut[1], dataOut[2], dataOut[3], dataOut[4], dataOut[5], dataOut[6], dataOut[7], dataOut[8], dataOut[9], dataOut[10], dataOut[11], dataOut[12], dataOut[13], dataOut[14], dataOut[15]);
endmodule

module Control (
  input  [3:0] Op,
  output RegDst,
  output Jump,
  output Branch,
  output MemToReg,
  output MemWrite,
  output ALUin,
  output RegWrite,
  output jal,
  output \input ,
  output \output 
);

  wire demultiplexer_1_out0, demultiplexer_1_out1, demultiplexer_1_out2, demultiplexer_1_out3,
       demultiplexer_1_out4, demultiplexer_1_out5, demultiplexer_1_out6, demultiplexer_1_out7,
       demultiplexer_1_out8, demultiplexer_1_out9, demultiplexer_1_out11, demultiplexer_1_out12,
       demultiplexer_1_out13;

  Demultiplexer #(.select(4), .enable("false")) demultiplexer_1 (
    .out0(demultiplexer_1_out0), .out1(demultiplexer_1_out1), .out2(demultiplexer_1_out2),
    .out3(demultiplexer_1_out3), .out4(demultiplexer_1_out4), .out5(demultiplexer_1_out5),
    .out6(demultiplexer_1_out6), .out7(demultiplexer_1_out7), .out8(demultiplexer_1_out8),
    .out9(demultiplexer_1_out9), .out10(jal), .out11(demultiplexer_1_out11), .out12(demultiplexer_1_out12),
    .out13(demultiplexer_1_out13), .out14(\input ), .out15(\output ), .in(1'b1), .sel(Op));
  or or_1 (RegDst, demultiplexer_1_out0, demultiplexer_1_out1, demultiplexer_1_out3, demultiplexer_1_out4, demultiplexer_1_out5, demultiplexer_1_out6, demultiplexer_1_out11, \input );
  or or_2 (Jump, demultiplexer_1_out9, jal, demultiplexer_1_out11);
  or or_3 (Branch, demultiplexer_1_out12, demultiplexer_1_out13);
  buf or_4 (MemToReg, demultiplexer_1_out7);  // OR_Gate
  buf or_5 (MemWrite, demultiplexer_1_out8);  // OR_Gate
  or or_6 (ALUin, demultiplexer_1_out2, demultiplexer_1_out5, demultiplexer_1_out6, demultiplexer_1_out7, demultiplexer_1_out8);
  or or_7 (RegWrite, demultiplexer_1_out0, demultiplexer_1_out1, demultiplexer_1_out2, demultiplexer_1_out3, demultiplexer_1_out4, demultiplexer_1_out5, demultiplexer_1_out6, demultiplexer_1_out7, \input );

  // Notes on the sheet:
  //   not
  //   xor
  //   addi
  //   add
  //   sub
  //   sra
  //   sll
  //   lw
  //   sw
  //   j
  //   jal
  //   jr
  //   bne
  //   blt
  //   input
  //   output
  //   0 = $rt, 1 = $rd
  //   0 = register, 1 = immediate
endmodule
